// Logisim project lab12.circ as structural Verilog
module main (
  input  bnegate,
  input  ainvert,
  input  [1:0] operation,
  input  carryin,
  input  a,
  input  less,
  input  b,
  input  in_8,
  input  in_9,
  input  in_10,
  input  in_11,
  input  in_12,
  input  in_13,
  input  in_14,
  input  in_15,
  input  in_16,
  input  in_17,
  input  in_18,
  input  in_19,
  input  in_20,
  input  in_21,
  input  in_22,
  input  in_23,
  input  in_24,
  input  in_25,
  input  in_26,
  input  in_27,
  input  in_28,
  input  in_29,
  input  in_30,
  input  in_31,
  input  in_32,
  input  in_33,
  input  in_34,
  input  in_35,
  input  in_36,
  input  in_37,
  input  in_38,
  input  in_39,
  input  in_40,
  input  in_41,
  input  in_42,
  input  in_43,
  input  in_44,
  input  in_45,
  input  in_46,
  input  in_47,
  input  in_48,
  input  in_49,
  input  in_50,
  input  in_51,
  input  in_52,
  input  in_53,
  input  in_54,
  input  in_55,
  input  in_56,
  input  in_57,
  input  in_58,
  input  in_59,
  input  in_60,
  input  in_61,
  input  in_62,
  input  in_63,
  input  in_64,
  input  in_65,
  input  in_66,
  input  in_67,
  input  in_68,
  input  in_69,
  input  in_70,
  input  in_71,
  input  in_72,
  input  in_73,
  input  in_74,
  input  in_75,
  input  in_76,
  input  in_77,
  input  in_78,
  input  in_79,
  input  in_80,
  input  in_81,
  input  in_82,
  input  in_83,
  input  in_84,
  input  in_85,
  input  in_86,
  input  in_87,
  input  in_88,
  input  in_89,
  input  in_90,
  input  in_91,
  input  in_92,
  input  in_93,
  input  in_94,
  input  in_95,
  input  in_96,
  input  in_97,
  input  in_98,
  input  in_99,
  input  in_100,
  output out_101,
  output out_102,
  output out_103,
  output out_104,
  output out_105,
  output out_106,
  output out_107,
  output out_108,
  output out_109,
  output out_110,
  output out_111,
  output out_112,
  output out_113,
  output out_114,
  output out_115,
  output out_116,
  output out_117,
  output out_118,
  output out_119,
  output out_120,
  output out_121,
  output out_122,
  output out_123,
  output out_124,
  output out_125,
  output out_126,
  output out_127,
  output out_128,
  output out_129,
  output out_130,
  output out_131,
  output out_132
);

  wire bit_alu_1_carry_out, bit_alu_2_carry_out, bit_alu_3_carry_out, bit_alu_4_carry_out,
       bit_alu_5_carry_out, bit_alu_6_carry_out, bit_alu_7_carry_out, bit_alu_8_carry_out,
       bit_alu_9_carry_out, bit_alu_10_carry_out, bit_alu_11_carry_out, bit_alu_12_carry_out,
       bit_alu_13_carry_out, bit_alu_14_carry_out, bit_alu_15_carry_out, bit_alu_16_carry_out,
       bit_alu_17_carry_out, bit_alu_18_carry_out, bit_alu_19_carry_out, bit_alu_20_carry_out,
       bit_alu_21_carry_out, bit_alu_22_carry_out, bit_alu_23_carry_out, bit_alu_24_carry_out,
       bit_alu_25_carry_out, bit_alu_26_carry_out, bit_alu_27_carry_out, bit_alu_28_carry_out,
       bit_alu_29_carry_out, bit_alu_30_carry_out, bit_alu_31_carry_out;

  bit_ALU bit_alu_1 (
    .a(a), .ainvert(bnegate), .less(less), .b(b), .bivert(ainvert), .operation(operation),
    .carry_in(carryin), .result(out_101), .carry_out(bit_alu_1_carry_out));
  bit_ALU bit_alu_2 (
    .a(in_8), .ainvert(bnegate), .less(in_9), .b(in_10), .bivert(ainvert), .operation(operation),
    .carry_in(bit_alu_1_carry_out), .result(out_102), .carry_out(bit_alu_2_carry_out));
  bit_ALU bit_alu_3 (
    .a(in_11), .ainvert(bnegate), .less(in_12), .b(in_13), .bivert(ainvert), .operation(operation),
    .carry_in(bit_alu_2_carry_out), .result(out_103), .carry_out(bit_alu_3_carry_out));
  bit_ALU bit_alu_4 (
    .a(in_14), .ainvert(bnegate), .less(in_15), .b(in_16), .bivert(ainvert), .operation(operation),
    .carry_in(bit_alu_3_carry_out), .result(out_104), .carry_out(bit_alu_4_carry_out));
  bit_ALU bit_alu_5 (
    .a(in_17), .ainvert(bnegate), .less(in_18), .b(in_19), .bivert(ainvert), .operation(operation),
    .carry_in(bit_alu_4_carry_out), .result(out_105), .carry_out(bit_alu_5_carry_out));
  bit_ALU bit_alu_6 (
    .a(in_20), .ainvert(bnegate), .less(in_21), .b(in_22), .bivert(ainvert), .operation(operation),
    .carry_in(bit_alu_5_carry_out), .result(out_106), .carry_out(bit_alu_6_carry_out));
  bit_ALU bit_alu_7 (
    .a(in_23), .ainvert(bnegate), .less(in_24), .b(in_25), .bivert(ainvert), .operation(operation),
    .carry_in(bit_alu_6_carry_out), .result(out_107), .carry_out(bit_alu_7_carry_out));
  bit_ALU bit_alu_8 (
    .a(in_26), .ainvert(bnegate), .less(in_27), .b(in_28), .bivert(ainvert), .operation(operation),
    .carry_in(bit_alu_7_carry_out), .result(out_108), .carry_out(bit_alu_8_carry_out));
  bit_ALU bit_alu_9 (
    .a(in_29), .ainvert(bnegate), .less(in_30), .b(in_31), .bivert(ainvert), .operation(operation),
    .carry_in(bit_alu_8_carry_out), .result(out_109), .carry_out(bit_alu_9_carry_out));
  bit_ALU bit_alu_10 (
    .a(in_32), .ainvert(bnegate), .less(in_33), .b(in_34), .bivert(ainvert), .operation(operation),
    .carry_in(bit_alu_9_carry_out), .result(out_110), .carry_out(bit_alu_10_carry_out));
  bit_ALU bit_alu_11 (
    .a(in_35), .ainvert(bnegate), .less(in_36), .b(in_37), .bivert(ainvert), .operation(operation),
    .carry_in(bit_alu_10_carry_out), .result(out_111), .carry_out(bit_alu_11_carry_out));
  bit_ALU bit_alu_12 (
    .a(in_38), .ainvert(bnegate), .less(in_39), .b(in_40), .bivert(ainvert), .operation(operation),
    .carry_in(bit_alu_11_carry_out), .result(out_112), .carry_out(bit_alu_12_carry_out));
  bit_ALU bit_alu_13 (
    .a(in_41), .ainvert(bnegate), .less(in_42), .b(in_43), .bivert(ainvert), .operation(operation),
    .carry_in(bit_alu_12_carry_out), .result(out_113), .carry_out(bit_alu_13_carry_out));
  bit_ALU bit_alu_14 (
    .a(in_44), .ainvert(bnegate), .less(in_45), .b(in_46), .bivert(ainvert), .operation(operation),
    .carry_in(bit_alu_13_carry_out), .result(out_114), .carry_out(bit_alu_14_carry_out));
  bit_ALU bit_alu_15 (
    .a(in_47), .ainvert(bnegate), .less(in_48), .b(in_49), .bivert(ainvert), .operation(operation),
    .carry_in(bit_alu_14_carry_out), .result(out_115), .carry_out(bit_alu_15_carry_out));
  bit_ALU bit_alu_16 (
    .a(in_50), .ainvert(bnegate), .less(in_51), .b(in_52), .bivert(ainvert), .operation(operation),
    .carry_in(bit_alu_15_carry_out), .result(out_116), .carry_out(bit_alu_16_carry_out));
  bit_ALU bit_alu_17 (
    .a(in_53), .ainvert(bnegate), .less(in_54), .b(in_55), .bivert(ainvert), .operation(operation),
    .carry_in(bit_alu_16_carry_out), .result(out_117), .carry_out(bit_alu_17_carry_out));
  bit_ALU bit_alu_18 (
    .a(in_56), .ainvert(bnegate), .less(in_57), .b(in_58), .bivert(ainvert), .operation(operation),
    .carry_in(bit_alu_17_carry_out), .result(out_118), .carry_out(bit_alu_18_carry_out));
  bit_ALU bit_alu_19 (
    .a(in_59), .ainvert(bnegate), .less(in_60), .b(in_61), .bivert(ainvert), .operation(operation),
    .carry_in(bit_alu_18_carry_out), .result(out_119), .carry_out(bit_alu_19_carry_out));
  bit_ALU bit_alu_20 (
    .a(in_62), .ainvert(bnegate), .less(in_63), .b(in_64), .bivert(ainvert), .operation(operation),
    .carry_in(bit_alu_19_carry_out), .result(out_120), .carry_out(bit_alu_20_carry_out));
  bit_ALU bit_alu_21 (
    .a(in_65), .ainvert(bnegate), .less(in_66), .b(in_67), .bivert(ainvert), .operation(operation),
    .carry_in(bit_alu_20_carry_out), .result(out_121), .carry_out(bit_alu_21_carry_out));
  bit_ALU bit_alu_22 (
    .a(in_68), .ainvert(bnegate), .less(in_69), .b(in_70), .bivert(ainvert), .operation(operation),
    .carry_in(bit_alu_21_carry_out), .result(out_122), .carry_out(bit_alu_22_carry_out));
  bit_ALU bit_alu_23 (
    .a(in_71), .ainvert(bnegate), .less(in_72), .b(in_73), .bivert(ainvert), .operation(operation),
    .carry_in(bit_alu_22_carry_out), .result(out_123), .carry_out(bit_alu_23_carry_out));
  bit_ALU bit_alu_24 (
    .a(in_74), .ainvert(bnegate), .less(in_75), .b(in_76), .bivert(ainvert), .operation(operation),
    .carry_in(bit_alu_23_carry_out), .result(out_124), .carry_out(bit_alu_24_carry_out));
  bit_ALU bit_alu_25 (
    .a(in_77), .ainvert(bnegate), .less(in_78), .b(in_79), .bivert(ainvert), .operation(operation),
    .carry_in(bit_alu_24_carry_out), .result(out_125), .carry_out(bit_alu_25_carry_out));
  bit_ALU bit_alu_26 (
    .a(in_80), .ainvert(bnegate), .less(in_81), .b(in_82), .bivert(ainvert), .operation(operation),
    .carry_in(bit_alu_25_carry_out), .result(out_126), .carry_out(bit_alu_26_carry_out));
  bit_ALU bit_alu_27 (
    .a(in_83), .ainvert(bnegate), .less(in_84), .b(in_85), .bivert(ainvert), .operation(operation),
    .carry_in(bit_alu_26_carry_out), .result(out_127), .carry_out(bit_alu_27_carry_out));
  bit_ALU bit_alu_28 (
    .a(in_86), .ainvert(bnegate), .less(in_87), .b(in_88), .bivert(ainvert), .operation(operation),
    .carry_in(bit_alu_27_carry_out), .result(out_128), .carry_out(bit_alu_28_carry_out));
  bit_ALU bit_alu_29 (
    .a(in_89), .ainvert(bnegate), .less(in_90), .b(in_91), .bivert(ainvert), .operation(operation),
    .carry_in(bit_alu_28_carry_out), .result(out_129), .carry_out(bit_alu_29_carry_out));
  bit_ALU bit_alu_30 (
    .a(in_92), .ainvert(bnegate), .less(in_93), .b(in_94), .bivert(ainvert), .operation(operation),
    .carry_in(bit_alu_29_carry_out), .result(out_130), .carry_out(bit_alu_30_carry_out));
  bit_ALU bit_alu_31 (
    .a(in_95), .ainvert(bnegate), .less(in_96), .b(in_97), .bivert(ainvert), .operation(operation),
    .carry_in(bit_alu_30_carry_out), .result(out_131), .carry_out(bit_alu_31_carry_out));
  bit_ALU bit_alu_32 (
    .a(in_98), .ainvert(bnegate), .less(in_99), .b(in_100), .bivert(ainvert), .operation(operation),
    .carry_in(bit_alu_31_carry_out), .result(out_132));  // open: carry_out
endmodule

module Dlatch (
  input  C,
  input  D,
  output Q,
  output Q1
);

  wire and_1_out, and_2_out, not_1_out, or_1_out, or_2_out;

  not not_1 (not_1_out, D);
  and and_1 (and_1_out, C, not_1_out);
  and and_2 (and_2_out, C, D);
  or or_1 (or_1_out, and_1_out, Q1);
  not not_2 (Q, or_1_out);
  or or_2 (or_2_out, Q, and_2_out);
  not not_3 (Q1, or_2_out);
endmodule

module DFlipFlop (
  input  D,
  input  C,
  output Q,
  output Q1
);

  wire dlatch_1_q, not_1_out;

  Dlatch dlatch_1 (.C(C), .D(D), .Q(dlatch_1_q));  // open: Q1
  not not_1 (not_1_out, C);
  Dlatch dlatch_2 (.C(not_1_out), .D(dlatch_1_q), .Q(Q), .Q1(Q1));
endmodule

module Registerr (
  input  clock,
  input  [31:0] in_2,
  output [31:0] out_3
);

  DFlipFlop dflipflop_1 (.D(in_2[0]), .C(clock), .Q(out_3[0]));  // open: Q1
  DFlipFlop dflipflop_2 (.D(in_2[1]), .C(clock), .Q(out_3[1]));  // open: Q1
  DFlipFlop dflipflop_3 (.D(in_2[2]), .C(clock), .Q(out_3[2]));  // open: Q1
  DFlipFlop dflipflop_4 (.D(in_2[3]), .C(clock), .Q(out_3[3]));  // open: Q1
  DFlipFlop dflipflop_5 (.D(in_2[4]), .C(clock), .Q(out_3[4]));  // open: Q1
  DFlipFlop dflipflop_6 (.D(in_2[5]), .C(clock), .Q(out_3[5]));  // open: Q1
  DFlipFlop dflipflop_7 (.D(in_2[6]), .C(clock), .Q(out_3[6]));  // open: Q1
  DFlipFlop dflipflop_8 (.D(in_2[7]), .C(clock), .Q(out_3[7]));  // open: Q1
  DFlipFlop dflipflop_9 (.D(in_2[8]), .C(clock), .Q(out_3[8]));  // open: Q1
  DFlipFlop dflipflop_10 (.D(in_2[9]), .C(clock), .Q(out_3[9]));  // open: Q1
  DFlipFlop dflipflop_11 (.D(in_2[10]), .C(clock), .Q(out_3[10]));  // open: Q1
  DFlipFlop dflipflop_12 (.D(in_2[11]), .C(clock), .Q(out_3[11]));  // open: Q1
  DFlipFlop dflipflop_13 (.D(in_2[12]), .C(clock), .Q(out_3[12]));  // open: Q1
  DFlipFlop dflipflop_14 (.D(in_2[13]), .C(clock), .Q(out_3[13]));  // open: Q1
  DFlipFlop dflipflop_15 (.D(in_2[14]), .C(clock), .Q(out_3[14]));  // open: Q1
  DFlipFlop dflipflop_16 (.D(in_2[15]), .C(clock), .Q(out_3[15]));  // open: Q1
  DFlipFlop dflipflop_17 (.D(in_2[16]), .C(clock), .Q(out_3[16]));  // open: Q1
  DFlipFlop dflipflop_18 (.D(in_2[17]), .C(clock), .Q(out_3[17]));  // open: Q1
  DFlipFlop dflipflop_19 (.D(in_2[18]), .C(clock), .Q(out_3[18]));  // open: Q1
  DFlipFlop dflipflop_20 (.D(in_2[19]), .C(clock), .Q(out_3[19]));  // open: Q1
  DFlipFlop dflipflop_21 (.D(in_2[20]), .C(clock), .Q(out_3[20]));  // open: Q1
  DFlipFlop dflipflop_22 (.D(in_2[21]), .C(clock), .Q(out_3[21]));  // open: Q1
  DFlipFlop dflipflop_23 (.D(in_2[22]), .C(clock), .Q(out_3[22]));  // open: Q1
  DFlipFlop dflipflop_24 (.D(in_2[23]), .C(clock), .Q(out_3[23]));  // open: Q1
  DFlipFlop dflipflop_25 (.D(in_2[24]), .C(clock), .Q(out_3[24]));  // open: Q1
  DFlipFlop dflipflop_26 (.D(in_2[25]), .C(clock), .Q(out_3[25]));  // open: Q1
  DFlipFlop dflipflop_27 (.D(in_2[26]), .C(clock), .Q(out_3[26]));  // open: Q1
  DFlipFlop dflipflop_28 (.D(in_2[27]), .C(clock), .Q(out_3[27]));  // open: Q1
  DFlipFlop dflipflop_29 (.D(in_2[28]), .C(clock), .Q(out_3[28]));  // open: Q1
  DFlipFlop dflipflop_30 (.D(in_2[29]), .C(clock), .Q(out_3[29]));  // open: Q1
  DFlipFlop dflipflop_31 (.D(in_2[30]), .C(clock), .Q(out_3[30]));  // open: Q1
  DFlipFlop dflipflop_32 (.D(in_2[31]), .C(clock), .Q(out_3[31]));  // open: Q1
endmodule

module RegisterFile (
  input  write,
  input  [4:0] regnum,
  input  [4:0] reg1,
  input  [4:0] reg2,
  input  [31:0] dataWrite,
  output [31:0] data1,
  output [31:0] data2
);

  wire and_1_out, and_2_out, and_3_out, and_4_out, and_5_out, and_6_out, and_7_out, and_8_out, and_9_out,
       and_10_out, and_11_out, and_12_out, and_13_out, and_14_out, and_15_out, and_16_out, and_17_out,
       and_18_out, and_19_out, and_20_out, and_21_out, and_22_out, and_23_out, and_24_out, and_25_out,
       and_26_out, and_27_out, and_28_out, and_29_out, and_30_out, and_31_out, and_32_out, decoder_1_out0,
       decoder_1_out1, decoder_1_out2, decoder_1_out3, decoder_1_out4, decoder_1_out5, decoder_1_out6,
       decoder_1_out7, decoder_1_out8, decoder_1_out9, decoder_1_out10, decoder_1_out11, decoder_1_out12,
       decoder_1_out13, decoder_1_out14, decoder_1_out15, decoder_1_out16, decoder_1_out17, decoder_1_out18,
       decoder_1_out19, decoder_1_out20, decoder_1_out21, decoder_1_out22, decoder_1_out23, decoder_1_out24,
       decoder_1_out25, decoder_1_out26, decoder_1_out27, decoder_1_out28, decoder_1_out29, decoder_1_out30,
       decoder_1_out31;
  wire [31:0] registerr_1_out_3, registerr_2_out_3, registerr_3_out_3, registerr_4_out_3, registerr_5_out_3,
       registerr_6_out_3, registerr_7_out_3, registerr_8_out_3, registerr_9_out_3, registerr_10_out_3,
       registerr_11_out_3, registerr_12_out_3, registerr_13_out_3, registerr_14_out_3, registerr_15_out_3,
       registerr_16_out_3, registerr_17_out_3, registerr_18_out_3, registerr_19_out_3, registerr_20_out_3,
       registerr_21_out_3, registerr_22_out_3, registerr_23_out_3, registerr_24_out_3, registerr_25_out_3,
       registerr_26_out_3, registerr_27_out_3, registerr_28_out_3, registerr_29_out_3, registerr_30_out_3,
       registerr_31_out_3, registerr_32_out_3;

  Decoder #(.enable("false"), .select(5)) decoder_1 (
    .out0(decoder_1_out0), .out1(decoder_1_out1), .out2(decoder_1_out2), .out3(decoder_1_out3),
    .out4(decoder_1_out4), .out5(decoder_1_out5), .out6(decoder_1_out6), .out7(decoder_1_out7),
    .out8(decoder_1_out8), .out9(decoder_1_out9), .out10(decoder_1_out10), .out11(decoder_1_out11),
    .out12(decoder_1_out12), .out13(decoder_1_out13), .out14(decoder_1_out14), .out15(decoder_1_out15),
    .out16(decoder_1_out16), .out17(decoder_1_out17), .out18(decoder_1_out18), .out19(decoder_1_out19),
    .out20(decoder_1_out20), .out21(decoder_1_out21), .out22(decoder_1_out22), .out23(decoder_1_out23),
    .out24(decoder_1_out24), .out25(decoder_1_out25), .out26(decoder_1_out26), .out27(decoder_1_out27),
    .out28(decoder_1_out28), .out29(decoder_1_out29), .out30(decoder_1_out30), .out31(decoder_1_out31),
    .sel(regnum));
  and and_1 (and_1_out, decoder_1_out0, write);
  and and_2 (and_2_out, decoder_1_out1, write);
  and and_3 (and_3_out, decoder_1_out2, write);
  and and_4 (and_4_out, decoder_1_out3, write);
  and and_5 (and_5_out, decoder_1_out4, write);
  and and_6 (and_6_out, decoder_1_out5, write);
  and and_7 (and_7_out, decoder_1_out6, write);
  and and_8 (and_8_out, decoder_1_out7, write);
  and and_9 (and_9_out, decoder_1_out8, write);
  and and_10 (and_10_out, decoder_1_out9, write);
  and and_11 (and_11_out, decoder_1_out10, write);
  and and_12 (and_12_out, decoder_1_out11, write);
  and and_13 (and_13_out, decoder_1_out12, write);
  and and_14 (and_14_out, decoder_1_out13, write);
  and and_15 (and_15_out, decoder_1_out14, write);
  and and_16 (and_16_out, decoder_1_out15, write);
  and and_17 (and_17_out, decoder_1_out16, write);
  and and_18 (and_18_out, decoder_1_out17, write);
  and and_19 (and_19_out, decoder_1_out18, write);
  and and_20 (and_20_out, decoder_1_out19, write);
  and and_21 (and_21_out, decoder_1_out20, write);
  and and_22 (and_22_out, decoder_1_out21, write);
  and and_23 (and_23_out, decoder_1_out22, write);
  and and_24 (and_24_out, decoder_1_out23, write);
  and and_25 (and_25_out, decoder_1_out24, write);
  and and_26 (and_26_out, decoder_1_out25, write);
  and and_27 (and_27_out, decoder_1_out26, write);
  and and_28 (and_28_out, decoder_1_out27, write);
  and and_29 (and_29_out, decoder_1_out28, write);
  and and_30 (and_30_out, decoder_1_out29, write);
  and and_31 (and_31_out, decoder_1_out30, write);
  and and_32 (and_32_out, decoder_1_out31, write);
  Registerr registerr_1 (.clock(and_1_out), .in_2(dataWrite), .out_3(registerr_1_out_3));
  Registerr registerr_2 (.clock(and_2_out), .in_2(dataWrite), .out_3(registerr_2_out_3));
  Registerr registerr_3 (.clock(and_3_out), .in_2(dataWrite), .out_3(registerr_3_out_3));
  Registerr registerr_4 (.clock(and_4_out), .in_2(dataWrite), .out_3(registerr_4_out_3));
  Registerr registerr_5 (.clock(and_5_out), .in_2(dataWrite), .out_3(registerr_5_out_3));
  Registerr registerr_6 (.clock(and_6_out), .in_2(dataWrite), .out_3(registerr_6_out_3));
  Registerr registerr_7 (.clock(and_7_out), .in_2(dataWrite), .out_3(registerr_7_out_3));
  Registerr registerr_8 (.clock(and_8_out), .in_2(dataWrite), .out_3(registerr_8_out_3));
  Registerr registerr_9 (.clock(and_9_out), .in_2(dataWrite), .out_3(registerr_9_out_3));
  Registerr registerr_10 (.clock(and_10_out), .in_2(dataWrite), .out_3(registerr_10_out_3));
  Registerr registerr_11 (.clock(and_11_out), .in_2(dataWrite), .out_3(registerr_11_out_3));
  Registerr registerr_12 (.clock(and_12_out), .in_2(dataWrite), .out_3(registerr_12_out_3));
  Registerr registerr_13 (.clock(and_13_out), .in_2(dataWrite), .out_3(registerr_13_out_3));
  Registerr registerr_14 (.clock(and_14_out), .in_2(dataWrite), .out_3(registerr_14_out_3));
  Registerr registerr_15 (.clock(and_15_out), .in_2(dataWrite), .out_3(registerr_15_out_3));
  Registerr registerr_16 (.clock(and_16_out), .in_2(dataWrite), .out_3(registerr_16_out_3));
  Registerr registerr_17 (.clock(and_17_out), .in_2(dataWrite), .out_3(registerr_17_out_3));
  Registerr registerr_18 (.clock(and_18_out), .in_2(dataWrite), .out_3(registerr_18_out_3));
  Registerr registerr_19 (.clock(and_19_out), .in_2(dataWrite), .out_3(registerr_19_out_3));
  Registerr registerr_20 (.clock(and_20_out), .in_2(dataWrite), .out_3(registerr_20_out_3));
  Registerr registerr_21 (.clock(and_21_out), .in_2(dataWrite), .out_3(registerr_21_out_3));
  Registerr registerr_22 (.clock(and_22_out), .in_2(dataWrite), .out_3(registerr_22_out_3));
  Registerr registerr_23 (.clock(and_23_out), .in_2(dataWrite), .out_3(registerr_23_out_3));
  Registerr registerr_24 (.clock(and_24_out), .in_2(dataWrite), .out_3(registerr_24_out_3));
  Registerr registerr_25 (.clock(and_25_out), .in_2(dataWrite), .out_3(registerr_25_out_3));
  Registerr registerr_26 (.clock(and_26_out), .in_2(dataWrite), .out_3(registerr_26_out_3));
  Registerr registerr_27 (.clock(and_27_out), .in_2(dataWrite), .out_3(registerr_27_out_3));
  Registerr registerr_28 (.clock(and_28_out), .in_2(dataWrite), .out_3(registerr_28_out_3));
  Registerr registerr_29 (.clock(and_29_out), .in_2(dataWrite), .out_3(registerr_29_out_3));
  Registerr registerr_30 (.clock(and_30_out), .in_2(dataWrite), .out_3(registerr_30_out_3));
  Registerr registerr_31 (.clock(and_31_out), .in_2(dataWrite), .out_3(registerr_31_out_3));
  Registerr registerr_32 (.clock(and_32_out), .in_2(dataWrite), .out_3(registerr_32_out_3));
  Multiplexer #(.select(5), .width(32)) multiplexer_1 (
    .in0(registerr_1_out_3), .in1(registerr_2_out_3), .in2(registerr_3_out_3), .in3(registerr_4_out_3),
    .in4(registerr_5_out_3), .in5(registerr_6_out_3), .in6(registerr_7_out_3), .in7(registerr_8_out_3),
    .in8(registerr_9_out_3), .in9(registerr_10_out_3), .in10(registerr_11_out_3), .in11(registerr_12_out_3),
    .in12(registerr_13_out_3), .in13(registerr_14_out_3), .in14(registerr_15_out_3),
    .in15(registerr_16_out_3), .in16(registerr_17_out_3), .in17(registerr_18_out_3),
    .in18(registerr_19_out_3), .in19(registerr_20_out_3), .in20(registerr_21_out_3),
    .in21(registerr_22_out_3), .in22(registerr_23_out_3), .in23(registerr_24_out_3),
    .in24(registerr_25_out_3), .in25(registerr_26_out_3), .in26(registerr_27_out_3),
    .in27(registerr_28_out_3), .in28(registerr_29_out_3), .in29(registerr_30_out_3),
    .in30(registerr_31_out_3), .in31(registerr_32_out_3), .out(data1), .sel(reg1));
  Multiplexer #(.select(5), .width(32)) multiplexer_2 (
    .in0(registerr_1_out_3), .in1(registerr_2_out_3), .in2(registerr_3_out_3), .in3(registerr_4_out_3),
    .in4(registerr_5_out_3), .in5(registerr_6_out_3), .in6(registerr_7_out_3), .in7(registerr_8_out_3),
    .in8(registerr_9_out_3), .in9(registerr_10_out_3), .in10(registerr_11_out_3), .in11(registerr_12_out_3),
    .in12(registerr_13_out_3), .in13(registerr_14_out_3), .in14(registerr_15_out_3),
    .in15(registerr_16_out_3), .in16(registerr_17_out_3), .in17(registerr_18_out_3),
    .in18(registerr_19_out_3), .in19(registerr_20_out_3), .in20(registerr_21_out_3),
    .in21(registerr_22_out_3), .in22(registerr_23_out_3), .in23(registerr_24_out_3),
    .in24(registerr_25_out_3), .in25(registerr_26_out_3), .in26(registerr_27_out_3),
    .in27(registerr_28_out_3), .in28(registerr_29_out_3), .in29(registerr_30_out_3),
    .in30(registerr_31_out_3), .in31(registerr_32_out_3), .out(data2), .sel(reg2));
endmodule

module ALUControl (
  input  [1:0] ALUOp0,
  input  [5:0] F,
  output [3:0] out_3
);

  wire and_1_out, not_1_out, not_2_out, not_3_out, or_1_out;

  or or_1 (or_1_out, F[3], F[0]);
  not not_1 (not_1_out, ALUOp0[0]);
  and and_1 (and_1_out, ALUOp0[1], F[1]);
  not not_2 (not_2_out, ALUOp0[1]);
  not not_3 (not_3_out, F[2]);
  and and_2 (out_3[3], ALUOp0[0], not_1_out);
  or or_2 (out_3[2], ALUOp0[0], and_1_out);
  or or_3 (out_3[1], not_2_out, not_3_out);
  and and_3 (out_3[0], ALUOp0[1], or_1_out);
endmodule

module MainControl (
  input  Op5,
  input  Op4,
  input  Op3,
  input  Op2,
  input  Op1,
  input  Op0,
  output RegDst,
  output ALUSrc,
  output MemroReg,
  output RegWrite,
  output MemRead,
  output MemWrite,
  output Branch,
  output ALUOp1,
  output ALUOp0
);

  wire not_1_out, not_2_out, not_3_out, not_4_out, not_5_out, not_6_out, not_7_out, not_8_out, not_9_out,
       not_10_out, not_11_out, not_12_out, not_13_out, not_14_out, not_15_out, not_16_out;

  not not_1 (not_1_out, Op0);
  not not_2 (not_2_out, Op1);
  not not_3 (not_3_out, Op2);
  not not_4 (not_4_out, Op3);
  not not_5 (not_5_out, Op4);
  and and_1 (ALUOp1, not_1_out, not_2_out, not_3_out, not_4_out, not_5_out, not_6_out);
  not not_6 (not_6_out, Op5);
  not not_7 (not_7_out, Op1);
  not not_8 (not_8_out, Op2);
  not not_9 (not_9_out, Op3);
  and and_2 (MemRead, Op0, not_7_out, not_8_out, not_9_out, Op4, Op5);
  not not_10 (not_10_out, Op1);
  not not_11 (not_11_out, Op3);
  and and_3 (MemWrite, Op0, not_10_out, Op2, not_11_out, Op4, Op5);
  not not_12 (not_12_out, Op0);
  not not_13 (not_13_out, Op1);
  not not_14 (not_14_out, Op2);
  not not_15 (not_15_out, Op4);
  not not_16 (not_16_out, Op5);
  and and_4 (ALUOp0, not_12_out, not_13_out, not_14_out, Op3, not_15_out, not_16_out);
  or or_1 (ALUSrc, MemRead, MemWrite);
  or or_2 (RegWrite, ALUOp1, MemRead);

  assign Branch = ALUOp0;
  assign MemroReg = MemRead;
  assign RegDst = ALUOp1;

  // Notes on the sheet:
  //   R-format
  //   lw
  //   sw
  //   beq
endmodule

module CPU (
);

  wire undriven;

  MainControl maincontrol_1 ();  // open: Op5, Op4, Op3, Op2, Op1, Op0, RegDst, ALUSrc, MemroReg, RegWrite, MemRead, MemWrite, Branch, ALUOp1, ALUOp0
  RegisterFile registerfile_1 (.write(undriven));  // open: regnum, reg1, reg2, dataWrite, data1, data2
endmodule

module adder_circuit (
  input  a,
  input  b,
  input  carry_in,
  output sum,
  output carry_out
);

  wire and_1_out, and_2_out, and_3_out, and_4_out, and_5_out, and_6_out, and_7_out, not_1_out, not_2_out,
       not_3_out;

  not not_1 (not_1_out, a);
  not not_2 (not_2_out, b);
  not not_3 (not_3_out, carry_in);
  and and_1 (and_1_out, not_1_out, not_2_out, carry_in);
  and and_2 (and_2_out, not_1_out, b, not_3_out);
  and and_3 (and_3_out, a, not_2_out, not_3_out);
  and and_4 (and_4_out, a, b, carry_in);
  and and_5 (and_5_out, b, carry_in);
  and and_6 (and_6_out, a, carry_in);
  and and_7 (and_7_out, a, b);
  or or_1 (sum, and_1_out, and_2_out, and_3_out, and_4_out);
  or or_2 (carry_out, and_5_out, and_6_out, and_7_out);
endmodule

module bit_ALU (
  input  a,
  input  ainvert,
  input  less,
  input  b,
  input  bivert,
  input  [1:0] operation,
  input  carry_in,
  output result,
  output carry_out
);

  wire adder_circuit_1_sum, and_1_out, multiplexer_1_out, multiplexer_2_out, not_1_out, not_2_out, or_1_out;

  not not_1 (not_1_out, a);
  not not_2 (not_2_out, b);
  Multiplexer multiplexer_1 (.in0(a), .in1(not_1_out), .out(multiplexer_1_out), .sel(ainvert));
  Multiplexer multiplexer_2 (.in0(b), .in1(not_2_out), .out(multiplexer_2_out), .sel(bivert));
  and and_1 (and_1_out, multiplexer_1_out, multiplexer_2_out);
  or or_1 (or_1_out, multiplexer_1_out, multiplexer_2_out);
  adder_circuit adder_circuit_1 (
    .a(multiplexer_1_out), .b(multiplexer_2_out), .carry_in(carry_in), .sum(adder_circuit_1_sum),
    .carry_out(carry_out));
  Multiplexer #(.select(2)) multiplexer_3 (
    .in0(and_1_out), .in1(or_1_out), .in2(adder_circuit_1_sum), .in3(less), .out(result), .sel(operation));
endmodule

module ALU (
  input  bnegate,
  input  ainvert,
  input  [1:0] operation,
  input  [31:0] operand2,
  input  [31:0] operand1,
  output [31:0] result,
  output zero
);

  wire or_1_out;

  main main_1 (
    .bnegate(bnegate), .ainvert(ainvert), .operation(operation), .carryin(1'b0), .a(operand1[0]),
    .b(operand2[0]), .in_8(operand1[1]), .in_10(operand2[1]), .in_11(operand1[2]), .in_13(operand2[2]),
    .in_14(operand1[3]), .in_16(operand2[3]), .in_17(operand1[4]), .in_19(operand2[4]), .in_20(operand1[5]),
    .in_22(operand2[5]), .in_23(operand1[6]), .in_25(operand2[6]), .in_26(operand1[7]), .in_28(operand2[7]),
    .in_29(operand1[8]), .in_31(operand2[8]), .in_32(operand1[9]), .in_33(operand2[9]), .in_35(operand1[10]),
    .in_37(operand2[10]), .in_38(operand1[11]), .in_40(operand2[11]), .in_41(operand1[12]),
    .in_43(operand2[12]), .in_44(operand1[13]), .in_46(operand2[13]), .in_47(operand1[14]),
    .in_49(operand2[14]), .in_50(operand1[15]), .in_52(operand2[15]), .in_53(operand1[16]),
    .in_55(operand2[16]), .in_56(operand1[17]), .in_58(operand2[17]), .in_59(operand1[18]),
    .in_61(operand2[18]), .in_62(operand1[19]), .in_64(operand2[19]), .in_65(operand1[20]),
    .in_67(operand2[20]), .in_68(operand1[21]), .in_70(operand2[21]), .in_71(operand1[22]),
    .in_73(operand2[22]), .in_74(operand1[23]), .in_76(operand2[23]), .in_77(operand1[24]),
    .in_79(operand2[24]), .in_80(operand1[25]), .in_82(operand2[25]), .in_83(operand1[26]),
    .in_85(operand2[26]), .in_86(operand1[27]), .in_88(operand2[27]), .in_89(operand1[28]),
    .in_91(operand2[28]), .in_92(operand1[29]), .in_94(operand2[29]), .in_95(operand1[30]),
    .in_97(operand2[30]), .in_98(operand1[31]), .in_100(operand2[31]), .out_101(result[0]),
    .out_102(result[1]), .out_103(result[2]), .out_104(result[3]), .out_105(result[4]), .out_106(result[5]),
    .out_107(result[6]), .out_108(result[7]), .out_109(result[8]), .out_110(result[9]), .out_111(result[10]),
    .out_112(result[11]), .out_113(result[12]), .out_114(result[13]), .out_115(result[14]),
    .out_116(result[15]), .out_117(result[16]), .out_118(result[17]), .out_119(result[18]),
    .out_120(result[19]), .out_121(result[20]), .out_122(result[21]), .out_123(result[22]),
    .out_124(result[23]), .out_125(result[24]), .out_126(result[25]), .out_127(result[26]),
    .out_128(result[27]), .out_129(result[28]), .out_130(result[29]), .out_131(result[30]),
    .out_132(result[31]));  // open: less, in_9, in_12, in_15, in_18, in_21, in_24, in_27, in_30, in_34, in_36, in_39, in_42, in_45, in_48, in_51, in_54, in_57, in_60, in_63, in_66, in_69, in_72, in_75, in_78, in_81, in_84, in_87, in_90, in_93, in_96, in_99
  or or_1 (or_1_out, result[0], result[1], result[2], result[3], result[4], result[5], result[6], result[7], result[8], result[9], result[10], result[11], result[12], result[13], result[14], result[15], result[16], result[17], result[18], result[19], result[20], result[21], result[22], result[23], result[24], result[25], result[26], result[27], result[28], result[29], result[30], result[31]);
  not not_1 (zero, or_1_out);
endmodule
