// Logisim project lab13.circ as structural Verilog
module ALUControl (
  input  [1:0] ALUOp0,
  input  [5:0] F,
  output [3:0] out_3
);

  wire and_1_out, not_1_out, not_2_out, not_3_out, or_1_out;

  or or_1 (or_1_out, F[3], F[0]);
  not not_1 (not_1_out, ALUOp0[0]);
  and and_1 (and_1_out, ALUOp0[1], F[1]);
  not not_2 (not_2_out, ALUOp0[1]);
  not not_3 (not_3_out, F[2]);
  and and_2 (out_3[3], ALUOp0[0], not_1_out);
  or or_2 (out_3[2], ALUOp0[0], and_1_out);
  or or_3 (out_3[1], not_2_out, not_3_out);
  and and_3 (out_3[0], ALUOp0[1], or_1_out);
endmodule

module MainControl (
  input  Op5,
  input  Op4,
  input  Op3,
  input  Op2,
  input  Op1,
  input  Op0,
  output RegDst,
  output ALUSrc,
  output MemroReg,
  output RegWrite,
  output MemRead,
  output MemWrite,
  output Branch,
  output ALUOp1,
  output ALUOp0
);

  wire not_1_out, not_2_out, not_3_out, not_4_out, not_5_out, not_6_out, not_7_out, not_8_out, not_9_out,
       not_10_out, not_11_out, not_12_out, not_13_out, not_14_out, not_15_out, not_16_out;

  not not_1 (not_1_out, Op0);
  not not_2 (not_2_out, Op1);
  not not_3 (not_3_out, Op2);
  not not_4 (not_4_out, Op3);
  not not_5 (not_5_out, Op4);
  and and_1 (ALUOp1, not_1_out, not_2_out, not_3_out, not_4_out, not_5_out, not_6_out);
  not not_6 (not_6_out, Op5);
  not not_7 (not_7_out, Op1);
  not not_8 (not_8_out, Op2);
  not not_9 (not_9_out, Op3);
  and and_2 (MemRead, Op0, not_7_out, not_8_out, not_9_out, Op4, Op5);
  not not_10 (not_10_out, Op1);
  not not_11 (not_11_out, Op3);
  and and_3 (MemWrite, Op0, not_10_out, Op2, not_11_out, Op4, Op5);
  not not_12 (not_12_out, Op0);
  not not_13 (not_13_out, Op1);
  not not_14 (not_14_out, Op2);
  not not_15 (not_15_out, Op4);
  not not_16 (not_16_out, Op5);
  and and_4 (ALUOp0, not_12_out, not_13_out, not_14_out, Op3, not_15_out, not_16_out);
  or or_1 (ALUSrc, MemRead, MemWrite);
  or or_2 (RegWrite, ALUOp1, MemRead);

  assign Branch = ALUOp0;
  assign MemroReg = MemRead;
  assign RegDst = ALUOp1;

  // Notes on the sheet:
  //   R-format
  //   lw
  //   sw
  //   beq
endmodule
