// Logisim project lab4.circ as structural Verilog: 1 circuit, main circuit main
module main (
);

  wire and_1_out, and_2_out, clk, clr_out, rd, rd_wrt_out, reset_out, wrt;
  wire [6:0] keyboard_1_data;
  wire [7:0] controlled_buffer_2_out, counter_1_q, ram_1_data;

  Clock clock_1 (.out(clk));
  Button reset (.out(reset_out));
  Counter counter_1 (.clr(reset_out), .clk(clk), .Q(counter_1_q));  // open: load, up, count, D, carry
  D_Flip_Flop d_ff_1 (.D(1'b1), .clk(rd_wrt_out), .Q(wrt), .Qn(rd));  // open: preset, reset
  Button rd_wrt (.out(rd_wrt_out));
  LED led_1 (.in(wrt));
  RAM #(.databus("bidir")) ram_1 (.addr(counter_1_q), .we(wrt), .oe(rd), .clk(clk), .data(ram_1_data));
  LED led_2 (.in(rd));
  and and_1 (and_1_out, wrt, clk);
  Keyboard keyboard_1 (.clk(and_1_out), .data(keyboard_1_data));  // open: re, clr, avail
  assign ram_1_data = wrt ? {1'b0, keyboard_1_data} : 8'bz;  // Controlled_Buffer controlled_buffer_1
  assign controlled_buffer_2_out = rd ? ram_1_data : 8'bz;  // Controlled_Buffer controlled_buffer_2
  TTY tty_1 (.data(controlled_buffer_2_out[6:0]), .clk(and_2_out), .clr(clr_out));  // open: we
  and and_2 (and_2_out, rd, clk);
  Button clr (.out(clr_out));
endmodule
